# Fritzing sketch 2024-11-17 Guitar Amp with LM386 IC PCB version (saved by Fritzing 1.0.2b)
# 18650 Li-ion Battery: CC-BY Dr Kristofer Chan, King's College London/Remote-research.org
circuit board: 6.05654cm x 2.09985cm
perfboards: 1

parts:
  IN_-_JACK_6_5mm = AMPHENOL - ACJS-MHDR [package=ACJS-MHDR]
  OUT_-_JACK_6_5mm = AMPHENOL - ACJS-MHDR [package=ACJS-MHDR]
  LM386 = LM386 [package=dip08]
  BAT1 = 18650 Li-ion Battery [package=battery-18650]
  Gain = female pin header, 2 pins [form="♀ (female)"]
  IN = female pin header, 2 pins [form="♀ (female)"]
  batt = female pin header, 2 pins [form="♀ (female)"]
  R4 = Resistor [tolerance=±5% power=0.25W resistance=10k package=THT]
  pot_vol = female pin header, 3 pins [form="♀ (female)"]
  led = female pin header, 2 pins [form="♀ (female)"]
  Volume = Rotary Potentiometer (Small) [maximum_resistance=10kΩ knob_status=50% power=0.5W package=THT]
  Gain_2 = Rotary Potentiometer (Small) [maximum_resistance=10kΩ knob_status=50% power=0.5W package=THT]
  Distorstion_switch = Taiway 100-SP-X-T1 SPDT Miniature Toggle Switch [part_number=100-SP-X-T1-0-0-B1-M2 package=THT]
  Dist = female pin header, 2 pins [form="♀ (female)"]
  R7 = Resistor [tolerance=±5% power=0.25W resistance=10 package=THT]
  OUT = female pin header, 3 pins [form="♀ (female)"]
  LED1 = LED - 3mm [color="Red (633nm)" current=0.030A package="3 mm [THT]"]
  C6 = Electrolytic Capacitor [capacitance=10µF voltage=35V package="100 mil [THT, electrolytic]"]
  C8 = Electrolytic Capacitor [capacitance=4.7µF voltage=35V package="100 mil [THT, electrolytic]"]
  C9 = Electrolytic Capacitor [capacitance=10µF voltage=35V package="100 mil [THT, electrolytic]"]
  C10 = Electrolytic Capacitor [capacitance=0.47mF voltage=35V package="100 mil [THT, electrolytic]"]
  S9012 = PNP-Transistor [package="TO92 [THT]"]
  R3 = Resistor [tolerance=±5% resistance=1000 power=0.25W package=THT]
  C7 = Electrolytic Capacitor [capacitance=0.47mF voltage=35V package="100 mil [THT, electrolytic]"]

nets:
  N1: IN_-_JACK_6_5mm.Ring_(5), OUT_-_JACK_6_5mm.Sleeve_(4), LM386.-IN, LM386.V-, BAT1.-, IN.pin1, batt.pin1, pot_vol.pin3, Volume.leg2, OUT.pin3, C8.-, C9.-, C10.-, S9012.C, R3.Pin_0
  N2: IN_-_JACK_6_5mm.Tip_(6), IN.pin2, pot_vol.pin1, Volume.leg1
  N3: OUT_-_JACK_6_5mm.Ring_(5), OUT_-_JACK_6_5mm.Tip_(6), R4.Pin_1, Distorstion_switch.L2, Dist.pin1, OUT.pin1, OUT.pin2, S9012.E
  N4: LM386.GAIN, Gain.pin2, Gain_2.leg2, C6.-
  N5: LM386.+IN, pot_vol.pin2, Volume.wiper
  N6: LM386.OUT, R7.Pin_0, C7.+
  N7: LM386.V+, BAT1.+, batt.pin2, R4.Pin_0, led.pin2, LED1.anode, C10.+
  N8: LM386.BP, C9.+
  N9: Gain.pin1, Gain_2.wiper, C6.+
  N10: led.pin1, LED1.cathode, R3.Pin_1
  N11: Distorstion_switch.COM, Dist.pin2, S9012.B, C7.-
  N12: R7.Pin_1, C8.+

notes:
  + -
  GND 5V
  + + -
  Guitar Amp
  by Hippo
  v1.00 2024
  Guitar Amp Hippo

custom parts:
  18650 Li-ion Battery: 18650 li-ion Battery Standard 18650 battery with interactive connectors Creative Common Attribution 4.0 International (CC-BY 4.0) license. Any use of this part requires attribution of Dr Kristofer Chan, Department of Geography, King's College London. Contact kristofer.chan [at] kcl.ac.uk OR kris [at] remote-research.org for further information.
